# Fritzing sketch 52Can (saved by Fritzing 0.9.4)
circuit board: 5cm x 5cm
breadboards: 1

parts:
  U3 = Header 12 [package=1x12_machine-pin-header_lock.004]
  U1 = Header 12 [package=1x12_machine-pin-header_lock.004]
  U2 = Header 12 [package=1x12_machine-pin-header_lock.004]
  U4 = Header 12 [package=1x12_machine-pin-header_lock.004]
  U5 = Header 12 [package=1x12_machine-pin-header_lock.004]

nets:
  N1: U3.1, U1.1
  N2: U3.2, U1.2
  N3: U3.3, U1.3
  N4: U3.4, U1.4
  N5: U3.5, U1.5
  N6: U3.6, U1.6
  N7: U3.7, U1.7
  N8: U3.8, U1.8
  N9: U3.9, U1.9
  N10: U3.10, U1.10
  N11: U3.11, U1.11
  N12: U3.12, U1.12
  N13: U2.1, U4.1, U5.1
  N14: U2.2, U4.2, U5.2
  N15: U2.3, U4.3
  N16: U2.4, U4.4
  N17: U2.5, U4.5
  N18: U2.6, U4.6
  N19: U2.7, U4.7
  N20: U2.8, U4.8
  N21: U2.9, U4.9
  N22: U2.10, U4.10
  N23: U2.11, U4.11
  N24: U2.12, U4.12
